// Logisim project TheLife.circ as structural Verilog: 6 circuits, main circuit main
module main (
);

  wire [14:0] show_module_1_out_1, show_module_1_out_2, show_module_1_out_3, show_module_1_out_4,
       show_module_1_out_5, show_module_1_out_6, show_module_1_out_7, show_module_1_out_8,
       show_module_1_out_9, show_module_1_out_10, show_module_1_out_11, show_module_1_out_12,
       show_module_1_out_13, show_module_1_out_14, show_module_1_out_15;

  DotMatrix #(.matrixcols(15), .matrixrows(15)) dotmatrix_1 (
    .col0(show_module_1_out_1), .col1(show_module_1_out_2), .col2(show_module_1_out_3),
    .col3(show_module_1_out_4), .col4(show_module_1_out_5), .col5(show_module_1_out_6),
    .col6(show_module_1_out_7), .col7(show_module_1_out_8), .col8(show_module_1_out_9),
    .col9(show_module_1_out_10), .col10(show_module_1_out_11), .col11(show_module_1_out_12),
    .col12(show_module_1_out_13), .col13(show_module_1_out_14), .col14(show_module_1_out_15));
  Show_module show_module_1 (
    .out_1(show_module_1_out_1), .out_2(show_module_1_out_2), .out_3(show_module_1_out_3),
    .out_4(show_module_1_out_4), .out_5(show_module_1_out_5), .out_6(show_module_1_out_6),
    .out_7(show_module_1_out_7), .out_8(show_module_1_out_8), .out_9(show_module_1_out_9),
    .out_10(show_module_1_out_10), .out_11(show_module_1_out_11), .out_12(show_module_1_out_12),
    .out_13(show_module_1_out_13), .out_14(show_module_1_out_14), .out_15(show_module_1_out_15));
endmodule

module Show_module (
  output [14:0] out_1,
  output [14:0] out_2,
  output [14:0] out_3,
  output [14:0] out_4,
  output [14:0] out_5,
  output [14:0] out_6,
  output [14:0] out_7,
  output [14:0] out_8,
  output [14:0] out_9,
  output [14:0] out_10,
  output [14:0] out_11,
  output [14:0] out_12,
  output [14:0] out_13,
  output [14:0] out_14,
  output [14:0] out_15
);
endmodule

module Cell (
  input  upper_center,
  input  upper_left,
  input  upper_right,
  input  left,
  input  right,
  input  bottom_left,
  input  bottom_right,
  input  bottom_center,
  input  tick,
  input  waspressed,
  output State
);

  State_manager state_manager_1 (
    .nb1(upper_center), .nb2(upper_left), .nb3(upper_right), .nb4(left), .nb5(right), .nb6(bottom_left),
    .nb7(bottom_right), .nb8(bottom_center), .user_s_hand(tick), .tick(waspressed), .State(State));
endmodule

module State_manager (
  input  nb1,
  input  nb2,
  input  nb3,
  input  nb4,
  input  nb5,
  input  nb6,
  input  nb7,
  input  nb8,
  input  user_s_hand,
  input  tick,
  output State
);

  wire and_1_out, and_2_out, and_3_out, and_4_out, not_1_out, not_2_out, not_3_out, not_4_out, or_1_out,
       or_2_out, or_3_out;
  wire [1:0] adder_1_out, adder_2_out, adder_3_out, adder_4_out, adder_5_out, adder_6_out;
  wire [2:0] adder_7_out;
  wire [2:2] adder_5_cout, adder_6_cout;

  Adder #(.width(1)) adder_1 (.a(nb1), .b(nb2), .out(adder_1_out[0]), .cout(adder_1_out[1]));  // open: cin
  Adder #(.width(1)) adder_2 (.a(nb3), .b(nb4), .out(adder_2_out[0]), .cout(adder_2_out[1]));  // open: cin
  Adder #(.width(1)) adder_3 (.a(nb5), .b(nb6), .out(adder_3_out[0]), .cout(adder_3_out[1]));  // open: cin
  Adder #(.width(1)) adder_4 (.a(nb7), .b(nb8), .out(adder_4_out[0]), .cout(adder_4_out[1]));  // open: cin
  Adder #(.width(2)) adder_5 (
    .a(adder_1_out), .b(adder_2_out), .out(adder_5_out), .cout(adder_5_cout[2]));  // open: cin
  Adder #(.width(2)) adder_6 (
    .a(adder_3_out), .b(adder_4_out), .out(adder_6_out), .cout(adder_6_cout[2]));  // open: cin
  Adder #(.width(3)) adder_7 (
    .a({adder_5_cout[2], adder_5_out}), .b({adder_6_cout[2], adder_6_out}), .out(adder_7_out));  // open: cin, cout
  not not_1 (not_1_out, adder_7_out[2]);
  not not_2 (not_2_out, adder_7_out[0]);
  and and_1 (and_1_out, adder_7_out[0], adder_7_out[1], not_1_out);
  and and_2 (and_2_out, not_1_out, adder_7_out[1], not_2_out);
  or or_1 (or_1_out, user_s_hand, tick);
  not not_3 (not_3_out, user_s_hand);
  or or_2 (or_2_out, and_1_out, and_2_out);
  not not_4 (not_4_out, State);
  and and_3 (and_3_out, or_2_out, not_3_out);
  and and_4 (and_4_out, user_s_hand, not_4_out);
  or or_3 (or_3_out, and_3_out, and_4_out);
  Register #(.width(1), .trigger("falling")) register_1 (.D(or_3_out), .Q(State), .clk(or_1_out));  // open: en, clr

  // Notes on the sheet:
  //   3 живые
  //   2 живые
  //   Команда на смену состояния
  //   Оживание по правилам + нет команд от юзера
  //   Отрицание для смены состояния
endmodule

module Displaying_cells (
);

  Cell cell_1 ();  // open: upper_center, upper_left, upper_right, left, right, bottom_left, bottom_right, bottom_center, tick, waspressed, State
endmodule

module Row_of_cells (
  input  Upper_1,
  input  Upper_2,
  input  Upper_3,
  input  Upper_4,
  input  Upper_5,
  input  Upper_6,
  input  Upper_7,
  input  Upper_8,
  input  Upper_9,
  input  Upper_10,
  input  Upper_11,
  input  Upper_12,
  input  Upper_13,
  input  Upper_14,
  input  Upper_15
);

  Cell cell_1 (.upper_center(Upper_1));  // open: upper_left, upper_right, left, right, bottom_left, bottom_right, bottom_center, tick, waspressed, State
  Cell cell_2 (.upper_center(Upper_2));  // open: upper_left, upper_right, left, right, bottom_left, bottom_right, bottom_center, tick, waspressed, State
  Cell cell_3 (.upper_center(Upper_3));  // open: upper_left, upper_right, left, right, bottom_left, bottom_right, bottom_center, tick, waspressed, State
  Cell cell_4 (.upper_center(Upper_4));  // open: upper_left, upper_right, left, right, bottom_left, bottom_right, bottom_center, tick, waspressed, State
  Cell cell_5 (.upper_center(Upper_5));  // open: upper_left, upper_right, left, right, bottom_left, bottom_right, bottom_center, tick, waspressed, State
  Cell cell_6 (.upper_center(Upper_6));  // open: upper_left, upper_right, left, right, bottom_left, bottom_right, bottom_center, tick, waspressed, State
  Cell cell_7 (.upper_center(Upper_7));  // open: upper_left, upper_right, left, right, bottom_left, bottom_right, bottom_center, tick, waspressed, State
  Cell cell_8 (.upper_center(Upper_8));  // open: upper_left, upper_right, left, right, bottom_left, bottom_right, bottom_center, tick, waspressed, State
  Cell cell_9 (.upper_center(Upper_9));  // open: upper_left, upper_right, left, right, bottom_left, bottom_right, bottom_center, tick, waspressed, State
  Cell cell_10 (.upper_center(Upper_10));  // open: upper_left, upper_right, left, right, bottom_left, bottom_right, bottom_center, tick, waspressed, State
  Cell cell_11 (.upper_center(Upper_11));  // open: upper_left, upper_right, left, right, bottom_left, bottom_right, bottom_center, tick, waspressed, State
  Cell cell_12 (.upper_center(Upper_12));  // open: upper_left, upper_right, left, right, bottom_left, bottom_right, bottom_center, tick, waspressed, State
  Cell cell_13 (.upper_center(Upper_13));  // open: upper_left, upper_right, left, right, bottom_left, bottom_right, bottom_center, tick, waspressed, State
  Cell cell_14 (.upper_center(Upper_14));  // open: upper_left, upper_right, left, right, bottom_left, bottom_right, bottom_center, tick, waspressed, State
  Cell cell_15 (.upper_center(Upper_15));  // open: upper_left, upper_right, left, right, bottom_left, bottom_right, bottom_center, tick, waspressed, State
endmodule
